// Logisim project Board.circ as structural Verilog: 5 circuits, main circuit chip
module chip (
  input  lose,
  input  win,
  input  reset,
  input  [4:0] lose_2,
  input  [4:0] win_2,
  input  [4:0] reset_2,
  output [4:0] board,
  output lose_3,
  output win_3,
  output reset_3
);

  wire or_1_out, or_2_out;
  wire [4:0] controlled_buffer_1_out;

  or or_1 (or_1_out, lose, win);
  assign controlled_buffer_1_out = lose ? lose_2 : 5'bz;  // Controlled_Buffer controlled_buffer_1
  assign controlled_buffer_1_out = win ? win_2 : 5'bz;  // Controlled_Buffer controlled_buffer_2
  assign controlled_buffer_1_out = reset ? reset_2 : 5'bz;  // Controlled_Buffer controlled_buffer_3
  Pull_Resistor pull_resistor_1 (.node(controlled_buffer_1_out));
  Register #(.width(5)) register_1 (.D(controlled_buffer_1_out), .en(1'b1), .Q(board), .clk(or_2_out));  // open: clr
  or or_2 (or_2_out, reset, or_1_out);

  assign lose_3 = lose;
  assign reset_3 = reset;
  assign win_3 = win;

  // Other names for the same wires on the sheet: l[4:0] = lose_2; r[4:0] = reset_2; w[4:0] = win_2

  // Notes on the sheet:
  //   lose: pull=down
  //   reset: pull=down
  //   win: pull=down
endmodule

module block1 (
  input  lose,
  input  win,
  input  reset,
  output [4:0] out_4,
  output [4:0] out_5,
  output [4:0] out_6,
  output [4:0] out_7,
  output [4:0] out_8,
  output [4:0] out_9,
  output [4:0] out_10,
  output [4:0] out_11,
  output lose_2,
  output win_2,
  output reset_2
);

  wire chip_1_lose_3, chip_1_reset_3, chip_1_win_3, chip_2_lose_3, chip_2_reset_3, chip_2_win_3,
       chip_3_lose_3, chip_3_reset_3, chip_3_win_3, chip_4_lose_3, chip_4_reset_3, chip_4_win_3,
       chip_5_lose_3, chip_5_reset_3, chip_5_win_3, chip_6_lose_3, chip_6_reset_3, chip_6_win_3,
       chip_7_lose_3, chip_7_reset_3, chip_7_win_3;

  chip chip_1 (
    .win(chip_2_win_3), .lose_3(chip_1_lose_3), .win_3(chip_1_win_3), .reset_3(chip_1_reset_3),
    .board(out_5), .reset(chip_2_reset_3), .lose(chip_2_lose_3), .win_2(5'b01100), .reset_2(5'b10000),
    .lose_2(5'b01100));
  chip chip_2 (
    .win(win), .lose_3(chip_2_lose_3), .win_3(chip_2_win_3), .reset_3(chip_2_reset_3), .board(out_4),
    .reset(reset), .lose(lose), .win_2(5'b11000), .reset_2(5'b10000), .lose_2(5'b11000));
  chip chip_3 (
    .win(chip_1_win_3), .lose_3(chip_3_lose_3), .win_3(chip_3_win_3), .reset_3(chip_3_reset_3),
    .board(out_6), .reset(chip_1_reset_3), .lose(chip_1_lose_3), .win_2(5'b00111), .reset_2({5{1'b1}}),
    .lose_2(5'b00111));
  chip chip_4 (
    .win(chip_3_win_3), .lose_3(chip_4_lose_3), .win_3(chip_4_win_3), .reset_3(chip_4_reset_3),
    .board(out_7), .reset(chip_3_reset_3), .lose(chip_3_lose_3), .win_2(5'b01100), .reset_2(5'b10000),
    .lose_2(5'b01100));
  chip chip_5 (
    .win(chip_4_win_3), .lose_3(chip_5_lose_3), .win_3(chip_5_win_3), .reset_3(chip_5_reset_3),
    .board(out_8), .reset(chip_4_reset_3), .lose(chip_4_lose_3), .win_2(5'b11000), .reset_2(5'b10000),
    .lose_2(5'b11000));
  chip chip_6 (
    .win(chip_5_win_3), .lose_3(chip_6_lose_3), .win_3(chip_6_win_3), .reset_3(chip_6_reset_3),
    .board(out_9), .reset(chip_5_reset_3), .lose(chip_5_lose_3), .win_2({5{1'b0}}), .reset_2({5{1'b0}}),
    .lose_2({5{1'b0}}));
  chip chip_7 (
    .win(chip_6_win_3), .lose_3(chip_7_lose_3), .win_3(chip_7_win_3), .reset_3(chip_7_reset_3),
    .board(out_10), .reset(chip_6_reset_3), .lose(chip_6_lose_3), .win_2({5{1'b1}}), .reset_2({5{1'b1}}),
    .lose_2({5{1'b1}}));
  chip chip_8 (
    .win(chip_7_win_3), .lose_3(lose_2), .win_3(win_2), .reset_3(reset_2), .board(out_11),
    .reset(chip_7_reset_3), .lose(chip_7_lose_3), .win_2(5'b10001), .reset_2(5'b10101), .lose_2(5'b10001));

  // Notes on the sheet:
  //   win_2: pull=down
  //   reset: pull=down
  //   lose_2: pull=down
  //   lose: pull=down
  //   win: pull=down
  //   reset_2: pull=down
endmodule

module block2 (
  input  lose,
  input  win,
  input  reset,
  output [4:0] out_4,
  output [4:0] out_5,
  output [4:0] out_6,
  output [4:0] out_7,
  output [4:0] out_8,
  output [4:0] out_9,
  output [4:0] out_10,
  output [4:0] out_11,
  output lose_2,
  output win_2,
  output reset_2
);

  wire chip_1_lose_3, chip_1_reset_3, chip_1_win_3, chip_2_lose_3, chip_2_reset_3, chip_2_win_3,
       chip_3_lose_3, chip_3_reset_3, chip_3_win_3, chip_4_lose_3, chip_4_reset_3, chip_4_win_3,
       chip_5_lose_3, chip_5_reset_3, chip_5_win_3, chip_6_lose_3, chip_6_reset_3, chip_6_win_3,
       chip_7_lose_3, chip_7_reset_3, chip_7_win_3;

  chip chip_1 (
    .win(chip_2_win_3), .lose_3(chip_1_lose_3), .win_3(chip_1_win_3), .reset_3(chip_1_reset_3),
    .board(out_5), .reset(chip_2_reset_3), .lose(chip_2_lose_3), .win_2({5{1'b0}}), .reset_2(5'b10101),
    .lose_2({5{1'b0}}));
  chip chip_2 (
    .win(win), .lose_3(chip_2_lose_3), .win_3(chip_2_win_3), .reset_3(chip_2_reset_3), .board(out_4),
    .reset(reset), .lose(lose), .win_2({5{1'b1}}), .reset_2(5'b10101), .lose_2({5{1'b1}}));
  chip chip_3 (
    .win(chip_1_win_3), .lose_3(chip_3_lose_3), .win_3(chip_3_win_3), .reset_3(chip_3_reset_3),
    .board(out_6), .reset(chip_1_reset_3), .lose(chip_1_lose_3), .win_2({5{1'b1}}), .reset_2({5{1'b0}}),
    .lose_2({5{1'b1}}));
  chip chip_4 (
    .win(chip_3_win_3), .lose_3(chip_4_lose_3), .win_3(chip_4_win_3), .reset_3(chip_4_reset_3),
    .board(out_7), .reset(chip_3_reset_3), .lose(chip_3_lose_3), .win_2(5'b00001), .reset_2({5{1'b1}}),
    .lose_2(5'b00001));
  chip chip_5 (
    .win(chip_4_win_3), .lose_3(chip_5_lose_3), .win_3(chip_5_win_3), .reset_3(chip_5_reset_3),
    .board(out_8), .reset(chip_4_reset_3), .lose(chip_4_lose_3), .win_2(5'b00001), .reset_2(5'b01000),
    .lose_2(5'b00001));
  chip chip_6 (
    .win(chip_5_win_3), .lose_3(chip_6_lose_3), .win_3(chip_6_win_3), .reset_3(chip_6_reset_3),
    .board(out_9), .reset(chip_5_reset_3), .lose(chip_5_lose_3), .win_2({5{1'b1}}), .reset_2(5'b00100),
    .lose_2({5{1'b1}}));
  chip chip_7 (
    .win(chip_6_win_3), .lose_3(chip_7_lose_3), .win_3(chip_7_win_3), .reset_3(chip_7_reset_3),
    .board(out_10), .reset(chip_6_reset_3), .lose(chip_6_lose_3), .win_2({5{1'b0}}), .reset_2(5'b00010),
    .lose_2({5{1'b0}}));
  chip chip_8 (
    .win(chip_7_win_3), .lose_3(lose_2), .win_3(win_2), .reset_3(reset_2), .board(out_11),
    .reset(chip_7_reset_3), .lose(chip_7_lose_3), .win_2({5{1'b0}}), .reset_2({5{1'b1}}), .lose_2({5{1'b0}}));
endmodule

module block3 (
  input  lose,
  input  win,
  input  reset,
  output [4:0] out_4,
  output [4:0] out_5,
  output [4:0] out_6,
  output [4:0] out_7,
  output [4:0] out_8,
  output [4:0] out_9,
  output [4:0] out_10,
  output [4:0] out_11,
  output lose_2,
  output win_2,
  output reset_2
);

  wire chip_1_lose_3, chip_1_reset_3, chip_1_win_3, chip_2_lose_3, chip_2_reset_3, chip_2_win_3,
       chip_3_lose_3, chip_3_reset_3, chip_3_win_3, chip_4_lose_3, chip_4_reset_3, chip_4_win_3,
       chip_5_lose_3, chip_5_reset_3, chip_5_win_3, chip_6_lose_3, chip_6_reset_3, chip_6_win_3,
       chip_7_lose_3, chip_7_reset_3, chip_7_win_3;

  chip chip_1 (
    .win(chip_2_win_3), .lose_3(chip_1_lose_3), .win_3(chip_1_win_3), .reset_3(chip_1_reset_3),
    .board(out_5), .reset(chip_2_reset_3), .lose(chip_2_lose_3), .win_2(5'b00010), .reset_2({5{1'b1}}),
    .lose_2(5'b00001));
  chip chip_2 (
    .win(win), .lose_3(chip_2_lose_3), .win_3(chip_2_win_3), .reset_3(chip_2_reset_3), .board(out_4),
    .reset(reset), .lose(lose), .win_2({5{1'b1}}), .reset_2({5{1'b0}}), .lose_2({5{1'b1}}));
  chip chip_3 (
    .win(chip_1_win_3), .lose_3(chip_3_lose_3), .win_3(chip_3_win_3), .reset_3(chip_3_reset_3),
    .board(out_6), .reset(chip_1_reset_3), .lose(chip_1_lose_3), .win_2(5'b00100), .reset_2(5'b01000),
    .lose_2(5'b00001));
  chip chip_4 (
    .win(chip_3_win_3), .lose_3(chip_4_lose_3), .win_3(chip_4_win_3), .reset_3(chip_4_reset_3),
    .board(out_7), .reset(chip_3_reset_3), .lose(chip_3_lose_3), .win_2(5'b00010), .reset_2(5'b00100),
    .lose_2({5{1'b0}}));
  chip chip_5 (
    .win(chip_6_win_3), .lose_3(chip_5_lose_3), .win_3(chip_5_win_3), .reset_3(chip_5_reset_3),
    .board(out_9), .reset(chip_6_reset_3), .lose(chip_6_lose_3), .win_2({5{1'b0}}), .reset_2({5{1'b1}}),
    .lose_2(5'b10001));
  chip chip_6 (
    .win(chip_4_win_3), .lose_3(chip_6_lose_3), .win_3(chip_6_win_3), .reset_3(chip_6_reset_3),
    .board(out_8), .reset(chip_4_reset_3), .lose(chip_4_lose_3), .win_2({5{1'b1}}), .reset_2(5'b00010),
    .lose_2({5{1'b1}}));
  chip chip_7 (
    .win(chip_5_win_3), .lose_3(chip_7_lose_3), .win_3(chip_7_win_3), .reset_3(chip_7_reset_3),
    .board(out_10), .reset(chip_5_reset_3), .lose(chip_5_lose_3), .win_2(5'b10001), .reset_2({5{1'b0}}),
    .lose_2({5{1'b1}}));
  chip chip_8 (
    .win(chip_7_win_3), .lose_3(lose_2), .win_3(win_2), .reset_3(reset_2), .board(out_11),
    .reset(chip_7_reset_3), .lose(chip_7_lose_3), .win_2({5{1'b1}}), .reset_2(5'b10001), .lose_2({5{1'b0}}));
endmodule

module block4 (
  input  lose,
  input  win,
  input  reset,
  output [4:0] out_4,
  output [4:0] out_5,
  output [4:0] out_6,
  output [4:0] out_7,
  output [4:0] out_8,
  output [4:0] out_9,
  output [4:0] out_10,
  output [4:0] out_11
);

  wire chip_1_lose_3, chip_1_reset_3, chip_1_win_3, chip_2_lose_3, chip_2_reset_3, chip_2_win_3,
       chip_3_lose_3, chip_3_reset_3, chip_3_win_3, chip_4_lose_3, chip_4_reset_3, chip_4_win_3,
       chip_5_lose_3, chip_5_reset_3, chip_5_win_3, chip_6_lose_3, chip_6_reset_3, chip_6_win_3,
       chip_7_lose_3, chip_7_reset_3, chip_7_win_3;

  chip chip_1 (
    .win(win), .lose_3(chip_1_lose_3), .win_3(chip_1_win_3), .reset_3(chip_1_reset_3), .board(out_4),
    .reset(reset), .lose(lose), .win_2(5'b10001), .reset_2({5{1'b1}}), .lose_2(5'b11101));
  chip chip_2 (
    .win(chip_1_win_3), .lose_3(chip_2_lose_3), .win_3(chip_2_win_3), .reset_3(chip_2_reset_3),
    .board(out_5), .reset(chip_1_reset_3), .lose(chip_1_lose_3), .win_2({5{1'b0}}), .reset_2(5'b10001),
    .lose_2(5'b10101));
  chip chip_3 (
    .win(chip_2_win_3), .lose_3(chip_3_lose_3), .win_3(chip_3_win_3), .reset_3(chip_3_reset_3),
    .board(out_6), .reset(chip_2_reset_3), .lose(chip_2_lose_3), .win_2({5{1'b1}}), .reset_2({5{1'b0}}),
    .lose_2(5'b10111));
  chip chip_4 (
    .win(chip_3_win_3), .lose_3(chip_4_lose_3), .win_3(chip_4_win_3), .reset_3(chip_4_reset_3),
    .board(out_7), .reset(chip_3_reset_3), .lose(chip_3_lose_3), .win_2(5'b01000), .reset_2(5'b11101),
    .lose_2({5{1'b0}}));
  chip chip_5 (
    .win(chip_6_win_3), .lose_3(chip_5_lose_3), .win_3(chip_5_win_3), .reset_3(chip_5_reset_3),
    .board(out_9), .reset(chip_6_reset_3), .lose(chip_6_lose_3), .win_2(5'b00010), .reset_2(5'b10101),
    .lose_2(5'b10101));
  chip chip_6 (
    .win(chip_4_win_3), .lose_3(chip_6_lose_3), .win_3(chip_6_win_3), .reset_3(chip_6_reset_3),
    .board(out_8), .reset(chip_4_reset_3), .lose(chip_4_lose_3), .win_2(5'b00100), .reset_2(5'b10101),
    .lose_2({5{1'b1}}));
  chip chip_7 (
    .win(chip_5_win_3), .lose_3(chip_7_lose_3), .win_3(chip_7_win_3), .reset_3(chip_7_reset_3),
    .board(out_10), .reset(chip_5_reset_3), .lose(chip_5_lose_3), .win_2({5{1'b1}}), .reset_2(5'b10111),
    .lose_2(5'b10101));
  chip chip_8 (
    .win(chip_7_win_3), .board(out_11), .reset(chip_7_reset_3), .lose(chip_7_lose_3), .win_2({5{1'b0}}),
    .reset_2({5{1'b0}}), .lose_2(5'b10101));  // open: lose_3, win_3, reset_3
endmodule
