// Logisim project Tennis.circ as structural Verilog: 5 circuits, main circuit chip
module main (
);

  wire block1_1_lose_2, block1_1_reset_2, block1_1_win_2, block2_1_lose_2, block2_1_reset_2, block2_1_win_2,
       block3_1_lose_2, block3_1_reset_2, block3_1_win_2, clock_1_out, clock_2_out, lose, reset, win;
  wire [3:0] n10_1_one, n10_1_ten, n10_2_one, n10_2_ten;
  wire [4:0] block1_1_out_4, block1_1_out_5, block1_1_out_6, block1_1_out_7, block1_1_out_8, block1_1_out_9,
       block1_1_out_10, block1_1_out_11, block2_1_out_4, block2_1_out_5, block2_1_out_6, block2_1_out_7,
       block2_1_out_8, block2_1_out_9, block2_1_out_10, block2_1_out_11, block3_1_out_4, block3_1_out_5,
       block3_1_out_6, block3_1_out_7, block3_1_out_8, block3_1_out_9, block3_1_out_10, block3_1_out_11,
       block4_1_out_4, block4_1_out_5, block4_1_out_6, block4_1_out_7, block4_1_out_8, block4_1_out_9,
       block4_1_out_10, block4_1_out_11, joystick_1_y, main_1_rightyin, main_2_ballx, main_2_bally,
       main_2_leftyout, main_2_rightyout, main_2_zero, not_1_out, videosystem_1_ballx_2,
       videosystem_1_bally_2, videosystem_1_chipid_2, videosystem_1_leftbaty_2, videosystem_1_rightbaty_2,
       videosystem_2_ballx_2, videosystem_2_bally_2, videosystem_2_chipid_2, videosystem_2_leftbaty_2,
       videosystem_2_rightbaty_2, videosystem_3_ballx_2, videosystem_3_bally_2, videosystem_3_chipid_2,
       videosystem_3_leftbaty_2, videosystem_3_rightbaty_2;
  wire [7:0] Ls, main_2_vxy, main_2_xball, main_2_yball, Rs;
  wire [31:0] videosystem_1_output, videosystem_1_output_2, videosystem_1_output_3, videosystem_1_output_4,
       videosystem_1_output_5, videosystem_1_output_6, videosystem_1_output_7, videosystem_1_output_8,
       videosystem_2_output, videosystem_2_output_2, videosystem_2_output_3, videosystem_2_output_4,
       videosystem_2_output_5, videosystem_2_output_6, videosystem_2_output_7, videosystem_2_output_8,
       videosystem_3_output, videosystem_3_output_2, videosystem_3_output_3, videosystem_3_output_4,
       videosystem_3_output_5, videosystem_3_output_6, videosystem_3_output_7, videosystem_3_output_8,
       videosystem_4_output, videosystem_4_output_2, videosystem_4_output_3, videosystem_4_output_4,
       videosystem_4_output_5, videosystem_4_output_6, videosystem_4_output_7, videosystem_4_output_8;

  Software_main main_1 (
    .rightYin(main_1_rightyin), .xball(main_2_xball), .yball(main_2_yball), .vxy(main_2_vxy),
    .bus_0(clock_1_out));
  Clock clock_1 (.out(clock_1_out));
  Hex_Digit_Display hex_digit_display_1 (.value(n10_1_ten));  // open: dp
  Hex_Digit_Display hex_digit_display_2 (.value(n10_1_one));  // open: dp
  _10 u_10_1 (.ten(n10_1_ten), .one(n10_1_one), .\input (Ls));
  Joystick #(.bits(5)) joystick_1 (.y(joystick_1_y));  // open: x
  Button R (.out(reset));
  assign not_1_out = ~joystick_1_y;  // NOT_Gate not_1, 5 bits wide
  Controller_main main_2 (
    .rightYin(main_1_rightyin), .xball(main_2_xball), .yball(main_2_yball), .vxy(main_2_vxy),
    .zero(main_2_zero), .ballX(main_2_ballx), .ballY(main_2_bally), .rightYout(main_2_rightyout),
    .leftYout(main_2_leftyout), .reset(reset), .leftYin(not_1_out), .scoreA(Rs), .scoreB(Ls),
    .clock(clock_2_out), .win(win), .lose(lose));
  Clock #(.highDuration(6), .lowDuration(6)) clock_2 (.out(clock_2_out));
  DotMatrix #(.matrixcols(32), .matrixrows(5)) dotmatrix_1 (
    .col0(block1_1_out_4), .col1(block1_1_out_5), .col2(block1_1_out_6), .col3(block1_1_out_7),
    .col4(block1_1_out_8), .col5(block1_1_out_9), .col6(block1_1_out_10), .col7(block1_1_out_11),
    .col8(block2_1_out_4), .col9(block2_1_out_5), .col10(block2_1_out_6), .col11(block2_1_out_7),
    .col12(block2_1_out_8), .col13(block2_1_out_9), .col14(block2_1_out_10), .col15(block2_1_out_11),
    .col16(block3_1_out_4), .col17(block3_1_out_5), .col18(block3_1_out_6), .col19(block3_1_out_7),
    .col20(block3_1_out_8), .col21(block3_1_out_9), .col22(block3_1_out_10), .col23(block3_1_out_11),
    .col24(block4_1_out_4), .col25(block4_1_out_5), .col26(block4_1_out_6), .col27(block4_1_out_7),
    .col28(block4_1_out_8), .col29(block4_1_out_9), .col30(block4_1_out_10), .col31(block4_1_out_11));
  block1 block1_1 (
    .lose(lose), .win(win), .reset(reset), .lose_2(block1_1_lose_2), .win_2(block1_1_win_2),
    .reset_2(block1_1_reset_2), .out_4(block1_1_out_4), .out_5(block1_1_out_5), .out_6(block1_1_out_6),
    .out_7(block1_1_out_7), .out_8(block1_1_out_8), .out_9(block1_1_out_9), .out_10(block1_1_out_10),
    .out_11(block1_1_out_11));
  DotMatrix #(.matrixcols(32), .matrixrows(32)) dotmatrix_2 (
    .col0(videosystem_1_output), .col1(videosystem_1_output_2), .col2(videosystem_1_output_3),
    .col3(videosystem_1_output_4), .col4(videosystem_1_output_5), .col5(videosystem_1_output_6),
    .col6(videosystem_1_output_7), .col7(videosystem_1_output_8), .col8(videosystem_2_output),
    .col9(videosystem_2_output_2), .col10(videosystem_2_output_3), .col11(videosystem_2_output_4),
    .col12(videosystem_2_output_5), .col13(videosystem_2_output_6), .col14(videosystem_2_output_7),
    .col15(videosystem_2_output_8), .col16(videosystem_3_output), .col17(videosystem_3_output_2),
    .col18(videosystem_3_output_3), .col19(videosystem_3_output_4), .col20(videosystem_3_output_5),
    .col21(videosystem_3_output_6), .col22(videosystem_3_output_7), .col23(videosystem_3_output_8),
    .col24(videosystem_4_output), .col25(videosystem_4_output_2), .col26(videosystem_4_output_3),
    .col27(videosystem_4_output_4), .col28(videosystem_4_output_5), .col29(videosystem_4_output_6),
    .col30(videosystem_4_output_7), .col31(videosystem_4_output_8));
  videosystem videosystem_1 (
    .chipID(main_2_zero), .ballX(main_2_ballx), .ballY(main_2_bally), .leftbatY(main_2_leftyout),
    .rightbatY(main_2_rightyout), .chipID_2(videosystem_1_chipid_2), .ballX_2(videosystem_1_ballx_2),
    .ballY_2(videosystem_1_bally_2), .leftbatY_2(videosystem_1_leftbaty_2),
    .rightbatY_2(videosystem_1_rightbaty_2), .\output (videosystem_1_output),
    .output_2(videosystem_1_output_2), .output_3(videosystem_1_output_3), .output_4(videosystem_1_output_4),
    .output_5(videosystem_1_output_5), .output_6(videosystem_1_output_6), .output_7(videosystem_1_output_7),
    .output_8(videosystem_1_output_8));
  block2 block2_1 (
    .lose(block1_1_lose_2), .win(block1_1_win_2), .reset(block1_1_reset_2), .lose_2(block2_1_lose_2),
    .win_2(block2_1_win_2), .reset_2(block2_1_reset_2), .out_4(block2_1_out_4), .out_5(block2_1_out_5),
    .out_6(block2_1_out_6), .out_7(block2_1_out_7), .out_8(block2_1_out_8), .out_9(block2_1_out_9),
    .out_10(block2_1_out_10), .out_11(block2_1_out_11));
  videosystem videosystem_2 (
    .chipID(videosystem_1_chipid_2), .ballX(videosystem_1_ballx_2), .ballY(videosystem_1_bally_2),
    .leftbatY(videosystem_1_leftbaty_2), .rightbatY(videosystem_1_rightbaty_2),
    .chipID_2(videosystem_2_chipid_2), .ballX_2(videosystem_2_ballx_2), .ballY_2(videosystem_2_bally_2),
    .leftbatY_2(videosystem_2_leftbaty_2), .rightbatY_2(videosystem_2_rightbaty_2),
    .\output (videosystem_2_output), .output_2(videosystem_2_output_2), .output_3(videosystem_2_output_3),
    .output_4(videosystem_2_output_4), .output_5(videosystem_2_output_5), .output_6(videosystem_2_output_6),
    .output_7(videosystem_2_output_7), .output_8(videosystem_2_output_8));
  block3 block3_1 (
    .lose(block2_1_lose_2), .win(block2_1_win_2), .reset(block2_1_reset_2), .lose_2(block3_1_lose_2),
    .win_2(block3_1_win_2), .reset_2(block3_1_reset_2), .out_4(block3_1_out_4), .out_5(block3_1_out_5),
    .out_6(block3_1_out_6), .out_7(block3_1_out_7), .out_8(block3_1_out_8), .out_9(block3_1_out_9),
    .out_10(block3_1_out_10), .out_11(block3_1_out_11));
  videosystem videosystem_3 (
    .chipID(videosystem_2_chipid_2), .ballX(videosystem_2_ballx_2), .ballY(videosystem_2_bally_2),
    .leftbatY(videosystem_2_leftbaty_2), .rightbatY(videosystem_2_rightbaty_2),
    .chipID_2(videosystem_3_chipid_2), .ballX_2(videosystem_3_ballx_2), .ballY_2(videosystem_3_bally_2),
    .leftbatY_2(videosystem_3_leftbaty_2), .rightbatY_2(videosystem_3_rightbaty_2),
    .\output (videosystem_3_output), .output_2(videosystem_3_output_2), .output_3(videosystem_3_output_3),
    .output_4(videosystem_3_output_4), .output_5(videosystem_3_output_5), .output_6(videosystem_3_output_6),
    .output_7(videosystem_3_output_7), .output_8(videosystem_3_output_8));
  block4 block4_1 (
    .lose(block3_1_lose_2), .win(block3_1_win_2), .reset(block3_1_reset_2), .out_4(block4_1_out_4),
    .out_5(block4_1_out_5), .out_6(block4_1_out_6), .out_7(block4_1_out_7), .out_8(block4_1_out_8),
    .out_9(block4_1_out_9), .out_10(block4_1_out_10), .out_11(block4_1_out_11));
  videosystem videosystem_4 (
    .chipID(videosystem_3_chipid_2), .ballX(videosystem_3_ballx_2), .ballY(videosystem_3_bally_2),
    .leftbatY(videosystem_3_leftbaty_2), .rightbatY(videosystem_3_rightbaty_2),
    .\output (videosystem_4_output), .output_2(videosystem_4_output_2), .output_3(videosystem_4_output_3),
    .output_4(videosystem_4_output_4), .output_5(videosystem_4_output_5), .output_6(videosystem_4_output_6),
    .output_7(videosystem_4_output_7), .output_8(videosystem_4_output_8));  // open: chipID_2, ballX_2, ballY_2, leftbatY_2, rightbatY_2
  Hex_Digit_Display hex_digit_display_3 (.value(n10_2_ten));  // open: dp
  Hex_Digit_Display hex_digit_display_4 (.value(n10_2_one));  // open: dp
  _10 u_10_2 (.ten(n10_2_ten), .one(n10_2_one), .\input (Rs));
endmodule

module videosystem (
  input  [4:0] chipID,
  input  [4:0] ballX,
  input  [4:0] ballY,
  input  [4:0] leftbatY,
  input  [4:0] rightbatY,
  output [31:0] \output ,
  output [31:0] output_2,
  output [31:0] output_3,
  output [31:0] output_4,
  output [31:0] output_5,
  output [31:0] output_6,
  output [31:0] output_7,
  output [31:0] output_8,
  output [4:0] chipID_2,
  output [4:0] ballX_2,
  output [4:0] ballY_2,
  output [4:0] leftbatY_2,
  output [4:0] rightbatY_2
);

  wire comparator_1_eq, comparator_2_eq;
  wire [4:0] chip_1_ballx_2, chip_1_bally_2, chip_1_chipid_2, chip_1_leftbaty_2, chip_1_rightbaty_2,
       chip_2_ballx_2, chip_2_bally_2, chip_2_chipid_2, chip_2_leftbaty_2, chip_2_rightbaty_2,
       chip_3_ballx_2, chip_3_bally_2, chip_3_chipid_2, chip_3_leftbaty_2, chip_3_rightbaty_2,
       chip_4_ballx_2, chip_4_bally_2, chip_4_chipid_2, chip_4_leftbaty_2, chip_4_rightbaty_2,
       chip_5_ballx_2, chip_5_bally_2, chip_5_chipid_2, chip_5_leftbaty_2, chip_5_rightbaty_2,
       chip_6_ballx_2, chip_6_bally_2, chip_6_chipid_2, chip_6_leftbaty_2, chip_6_rightbaty_2,
       chip_7_ballx_2, chip_7_bally_2, chip_7_chipid_2, chip_7_leftbaty_2, chip_7_rightbaty_2;
  wire [31:0] chip_2_output, chip_8_output, multiplexer_1_out, multiplexer_2_out;

  Comparator #(.width(5)) comparator_1 (.a(5'b10001), .b(chip_2_chipid_2), .eq(comparator_1_eq));  // open: gt, lt
  Multiplexer #(.width(32), .enable("false")) multiplexer_1 (
    .in0({32{1'b0}}), .in1(32'haaaaaaaa), .out(multiplexer_1_out), .sel(comparator_1_eq));
  assign \output  = multiplexer_1_out | chip_2_output;  // OR_Gate or_1, 32 bits wide
  chip chip_1 (
    .chipID(chip_2_chipid_2), .ballX(chip_2_ballx_2), .ballY(chip_2_bally_2), .leftbatY(chip_2_leftbaty_2),
    .rightbatY(chip_2_rightbaty_2), .\output (output_2), .chipID_2(chip_1_chipid_2),
    .ballX_2(chip_1_ballx_2), .ballY_2(chip_1_bally_2), .leftbatY_2(chip_1_leftbaty_2),
    .rightbatY_2(chip_1_rightbaty_2));
  chip chip_2 (
    .chipID(chipID), .ballX(ballX), .ballY(ballY), .leftbatY(leftbatY), .rightbatY(rightbatY),
    .\output (chip_2_output), .chipID_2(chip_2_chipid_2), .ballX_2(chip_2_ballx_2), .ballY_2(chip_2_bally_2),
    .leftbatY_2(chip_2_leftbaty_2), .rightbatY_2(chip_2_rightbaty_2));
  chip chip_3 (
    .chipID(chip_1_chipid_2), .ballX(chip_1_ballx_2), .ballY(chip_1_bally_2), .leftbatY(chip_1_leftbaty_2),
    .rightbatY(chip_1_rightbaty_2), .\output (output_3), .chipID_2(chip_3_chipid_2),
    .ballX_2(chip_3_ballx_2), .ballY_2(chip_3_bally_2), .leftbatY_2(chip_3_leftbaty_2),
    .rightbatY_2(chip_3_rightbaty_2));
  chip chip_4 (
    .chipID(chip_3_chipid_2), .ballX(chip_3_ballx_2), .ballY(chip_3_bally_2), .leftbatY(chip_3_leftbaty_2),
    .rightbatY(chip_3_rightbaty_2), .\output (output_4), .chipID_2(chip_4_chipid_2),
    .ballX_2(chip_4_ballx_2), .ballY_2(chip_4_bally_2), .leftbatY_2(chip_4_leftbaty_2),
    .rightbatY_2(chip_4_rightbaty_2));
  chip chip_5 (
    .chipID(chip_4_chipid_2), .ballX(chip_4_ballx_2), .ballY(chip_4_bally_2), .leftbatY(chip_4_leftbaty_2),
    .rightbatY(chip_4_rightbaty_2), .\output (output_5), .chipID_2(chip_5_chipid_2),
    .ballX_2(chip_5_ballx_2), .ballY_2(chip_5_bally_2), .leftbatY_2(chip_5_leftbaty_2),
    .rightbatY_2(chip_5_rightbaty_2));
  chip chip_6 (
    .chipID(chip_5_chipid_2), .ballX(chip_5_ballx_2), .ballY(chip_5_bally_2), .leftbatY(chip_5_leftbaty_2),
    .rightbatY(chip_5_rightbaty_2), .\output (output_6), .chipID_2(chip_6_chipid_2),
    .ballX_2(chip_6_ballx_2), .ballY_2(chip_6_bally_2), .leftbatY_2(chip_6_leftbaty_2),
    .rightbatY_2(chip_6_rightbaty_2));
  chip chip_7 (
    .chipID(chip_6_chipid_2), .ballX(chip_6_ballx_2), .ballY(chip_6_bally_2), .leftbatY(chip_6_leftbaty_2),
    .rightbatY(chip_6_rightbaty_2), .\output (output_7), .chipID_2(chip_7_chipid_2),
    .ballX_2(chip_7_ballx_2), .ballY_2(chip_7_bally_2), .leftbatY_2(chip_7_leftbaty_2),
    .rightbatY_2(chip_7_rightbaty_2));
  Comparator #(.width(5)) comparator_2 (.a(5'b10000), .b(chipID_2), .eq(comparator_2_eq));  // open: gt, lt
  chip chip_8 (
    .chipID(chip_7_chipid_2), .ballX(chip_7_ballx_2), .ballY(chip_7_bally_2), .leftbatY(chip_7_leftbaty_2),
    .rightbatY(chip_7_rightbaty_2), .\output (chip_8_output), .chipID_2(chipID_2), .ballX_2(ballX_2),
    .ballY_2(ballY_2), .leftbatY_2(leftbatY_2), .rightbatY_2(rightbatY_2));
  assign output_8 = multiplexer_2_out | chip_8_output;  // OR_Gate or_2, 32 bits wide
  Multiplexer #(.width(32), .enable("false")) multiplexer_2 (
    .in0({32{1'b0}}), .in1(32'h55555555), .out(multiplexer_2_out), .sel(comparator_2_eq));
endmodule

module chip (
  input  [4:0] chipID,
  input  [4:0] ballX,
  input  [4:0] ballY,
  input  [4:0] leftbatY,
  input  [4:0] rightbatY,
  output [31:0] \output ,
  output [4:0] chipID_2,
  output [4:0] ballX_2,
  output [4:0] ballY_2,
  output [4:0] leftbatY_2,
  output [4:0] rightbatY_2
);

  wire comparator_1_eq, comparator_2_eq, comparator_3_eq;
  wire [31:0] multiplexer_1_out, multiplexer_2_out, multiplexer_3_out, shifter_1_out, shifter_2_out,
       shifter_3_out;

  Multiplexer #(.width(32), .enable("false")) multiplexer_1 (
    .in0({32{1'b0}}), .in1(shifter_1_out), .out(multiplexer_1_out), .sel(comparator_1_eq));
  Comparator #(.width(5)) comparator_1 (.a(chipID), .b(ballX), .eq(comparator_1_eq));  // open: gt, lt
  Shifter #(.width(32)) shifter_1 (.in(32'h1), .\dist (ballY), .out(shifter_1_out));
  Comparator #(.width(5)) comparator_2 (.a(5'b00011), .b(chipID), .eq(comparator_2_eq));  // open: gt, lt
  Shifter #(.width(32)) shifter_2 (.in(32'h7), .\dist (leftbatY), .out(shifter_2_out));
  Comparator #(.width(5)) comparator_3 (.a(5'b11100), .b(chipID), .eq(comparator_3_eq));  // open: gt, lt
  Shifter #(.width(32)) shifter_3 (.in(32'h7), .\dist (rightbatY), .out(shifter_3_out));
  assign \output  = multiplexer_1_out | multiplexer_2_out | multiplexer_3_out;  // OR_Gate or_1, 32 bits wide
  Multiplexer #(.width(32), .enable("false")) multiplexer_2 (
    .in0({32{1'b0}}), .in1(shifter_2_out), .out(multiplexer_2_out), .sel(comparator_2_eq));
  Multiplexer #(.width(32), .enable("false")) multiplexer_3 (
    .in0({32{1'b0}}), .in1(shifter_3_out), .out(multiplexer_3_out), .sel(comparator_3_eq));
  inc inc_1 (.X(chipID), .R(chipID_2));

  assign ballX_2 = ballX;
  assign ballY_2 = ballY;
  assign leftbatY_2 = leftbatY;
  assign rightbatY_2 = rightbatY;
endmodule

module inc (
  input  [4:0] X,
  output [4:0] R
);

  wire [4:1] and_1_out;
  wire [4:4] and_1_out_2;

  assign {and_1_out_2[4], and_1_out} = {and_1_out, 1'b1} & X;  // AND_Gate and_1, 5 bits wide
  assign R = X ^ {and_1_out, 1'b1};  // XOR_Gate xor_1, 5 bits wide
  // Probe on and_1_out_2[4]
endmodule

module _10 (
  input  [7:0] \input ,
  output [3:0] ten,
  output [3:0] one
);

  wire [7:3] divider_1_out;
  wire [7:4] divider_1_rem;

  // Probe on \input 
  // Probe on {1'b0, ten[2:0]}
  Divider divider_1 (
    .a({4'b0000, \input [3:0]}), .b(8'ha), .out({divider_1_out, ten[2:0]}), .upper({\input [7:4], 4'b0000}),
    .rem({divider_1_rem, one}));
  // Probe on one

  assign ten[3] = 1'b0;
endmodule
